// Logisim project ZUOYE.circ as structural Verilog: 1 circuit, main circuit main
module main (
  input  KB,
  input  KL,
  input  KR,
  input  KS
);

  wire and_1_out, and_2_out, and_3_out, and_4_out, and_5_out, and_6_out, and_7_out, and_8_out, and_9_out,
       and_10_out, clock_1_out, clock_2_out, j_k_ff_1_q, j_k_ff_2_q, j_k_ff_3_q, j_k_ff_4_q, not_1_out,
       not_2_out, not_3_out, not_4_out, or_1_out, or_2_out, or_3_out, or_4_out, or_5_out, or_6_out, or_7_out,
       or_8_out, or_9_out, or_10_out, or_11_out, or_12_out, or_13_out, or_14_out, or_15_out, or_16_out,
       or_17_out, or_18_out, or_19_out, or_20_out, t_ff_1_q, t_ff_1_qn, t_ff_2_q, t_ff_2_qn;

  Clock clock_1 (.out(clock_1_out));
  Clock #(.highDuration(10)) clock_2 (.out(clock_2_out));
  and and_1 (and_1_out, KS, clock_1_out);
  and and_2 (and_2_out, KR, KL, KB);
  not not_1 (not_1_out, KL);
  T_Flip_Flop t_ff_1 (.T(1'b1), .clk(clock_2_out), .Q(t_ff_1_q), .Qn(t_ff_1_qn));  // open: reset, preset
  J_K_Flip_Flop j_k_ff_1 (.J(t_ff_1_qn), .K(t_ff_1_qn), .clk(clock_2_out), .Q(j_k_ff_1_q));  // open: Qn, preset, reset
  J_K_Flip_Flop j_k_ff_2 (.J(or_1_out), .K(not_2_out), .clk(clock_2_out), .Q(j_k_ff_2_q));  // open: Qn, preset, reset
  not not_2 (not_2_out, or_1_out);
  not not_3 (not_3_out, KR);
  not not_4 (not_4_out, or_2_out);
  T_Flip_Flop t_ff_2 (.T(1'b1), .clk(clock_2_out), .Q(t_ff_2_q), .Qn(t_ff_2_qn));  // open: reset, preset
  J_K_Flip_Flop j_k_ff_3 (.J(t_ff_2_qn), .K(t_ff_2_qn), .clk(clock_2_out), .Q(j_k_ff_3_q));  // open: Qn, preset, reset
  J_K_Flip_Flop j_k_ff_4 (.J(or_2_out), .K(not_4_out), .clk(clock_2_out), .Q(j_k_ff_4_q));  // open: Qn, preset, reset
  and and_3 (and_3_out, KB, not_1_out);
  and and_4 (and_4_out, KB, not_3_out);
  and and_5 (and_5_out, KL, t_ff_1_q);
  and and_6 (and_6_out, KL, j_k_ff_1_q);
  or or_1 (or_1_out, t_ff_1_qn, j_k_ff_1_q);
  and and_7 (and_7_out, j_k_ff_2_q, KL);
  and and_8 (and_8_out, KR, t_ff_2_q);
  and and_9 (and_9_out, KR, j_k_ff_3_q);
  or or_2 (or_2_out, t_ff_2_qn, j_k_ff_3_q);
  and and_10 (and_10_out, j_k_ff_4_q, KR);
  or or_3 (or_3_out, and_3_out, and_5_out);
  or or_4 (or_4_out, and_3_out, and_6_out);
  or or_5 (or_5_out, and_3_out, and_7_out);
  or or_6 (or_6_out, and_4_out, and_8_out);
  or or_7 (or_7_out, and_4_out, and_9_out);
  or or_8 (or_8_out, and_4_out, and_10_out);
  or or_9 (or_9_out, or_3_out, and_2_out);
  or or_10 (or_10_out, or_4_out, and_2_out);
  or or_11 (or_11_out, or_5_out, and_2_out);
  or or_12 (or_12_out, or_6_out, and_2_out);
  or or_13 (or_13_out, or_7_out, and_2_out);
  or or_14 (or_14_out, or_8_out, and_2_out);
  or or_15 (or_15_out, and_1_out, or_9_out);
  LED L1 (.in(or_15_out));
  LED L2 (.in(or_16_out));
  or or_16 (or_16_out, and_1_out, or_10_out);
  or or_17 (or_17_out, and_1_out, or_11_out);
  LED L3 (.in(or_17_out));
  LED R1 (.in(or_18_out));
  or or_18 (or_18_out, and_1_out, or_12_out);
  or or_19 (or_19_out, and_1_out, or_13_out);
  LED R2 (.in(or_19_out));
  or or_20 (or_20_out, or_14_out, and_1_out);
  LED R3 (.in(or_20_out));

  // Notes on the sheet:
  //   KB: initial=0x1
endmodule
